// Logisim project cpu.circ as structural Verilog: 1 circuit, main circuit main
module main (
  output [7:0] out_1,
  output [7:0] out_2,
  output [7:0] out_3,
  output [7:0] out_4,
  output [7:0] out_5,
  output [7:0] out_6,
  output [7:0] out_7,
  output [7:0] out_8
);

  wire clk, ENABLE_R0, ENABLE_R1, ENABLE_R2, ENABLE_R3, ENABLE_R4, ENABLE_R5, PC_READ, PC_WRITE;
  wire [7:0] MAIN_BUS, or_1_out, or_2_out, R0_JOY_SET, R0_SET;
  wire [15:0] bit_extender_1_out, PC_OUT;

  Clock clock_1 (.out(clk));
  assign or_1_out = MAIN_BUS | R0_SET;  // OR_Gate or_1, 8 bits wide
  assign or_2_out = R0_JOY_SET | MAIN_BUS | R0_SET;  // OR_Gate or_2, 8 bits wide
  Register register_1 (.D(or_2_out), .en(ENABLE_R0), .clk(clk), .Q(out_1));  // open: clr
  Register register_2 (.D(or_1_out), .en(ENABLE_R1), .clk(clk), .Q(out_2));  // open: clr
  Register register_3 (.D(MAIN_BUS), .en(ENABLE_R2), .clk(clk), .Q(out_3));  // open: clr
  Register register_4 (.D(MAIN_BUS), .en(ENABLE_R3), .clk(clk), .Q(out_4));  // open: clr
  Register register_5 (.D(MAIN_BUS), .en(ENABLE_R4), .clk(clk), .Q(out_5));  // open: clr
  Register register_6 (.D(MAIN_BUS), .en(ENABLE_R5), .clk(clk), .Q(out_6));  // open: clr
  Register register_7 (.D(MAIN_BUS), .en(ENABLE_R0), .clk(clk), .Q(out_7));  // open: clr
  Register register_8 (.D(MAIN_BUS), .en(ENABLE_R0), .clk(clk), .Q(out_8));  // open: clr
  Counter #(.max('hffff), .width(16)) counter_1 (
    .load(PC_WRITE), .clk(clk), .D({out_7, out_8}), .Q(PC_OUT));  // open: clr, up, count, carry
  ROM #(.addrWidth(16)) rom_1 (.addr(PC_OUT));  // open: data
  // AND_Gate and_1 has open pins: in0=PC_OUT, in1=bit_extender_1_out, out=open
  assign bit_extender_1_out = {{15{PC_READ}}, PC_READ};  // Bit_Extender bit_extender_1

  // Other names for the same wires on the sheet: R7[7:0] = out_8; R6[7:0] = out_7; R0[7:0] = out_1; R1[7:0] = out_2;
  //   R2[7:0] = out_3; R3[7:0] = out_4; R4[7:0] = out_5; R5[7:0] = out_6
endmodule
